// Logisim project spm.circ as structural Verilog: 3 circuits, main circuit main
module main (
  input  [7:0] in_1,
  input  [7:0] in_2,
  input  reset,
  output [6:0] out_4
);

  wire and_1_out, and_2_out, and_3_out, and_4_out, and_5_out, and_6_out, and_7_out, and_8_out, Clock1_out,
       csadder_1_sum, csadder_2_sum, csadder_3_sum, csadder_4_sum, csadder_5_sum, csadder_6_sum, tcmp_1_s;

  Clock Clock1 (.out(Clock1_out));
  and and_1 (and_1_out, in_2[7], in_1[7]);
  and and_2 (and_2_out, in_2[6], in_1[6]);
  TCMP tcmp_1 (.x(and_1_out), .clk(Clock1_out), .reset(reset), .S(tcmp_1_s));
  and and_3 (and_3_out, in_2[5], in_1[5]);
  CSAdder csadder_1 (.A(and_2_out), .B(tcmp_1_s), .clk(Clock1_out), .reset(reset), .Sum(csadder_1_sum), .Ci(out_4[6]));
  and and_4 (and_4_out, in_2[4], in_1[4]);
  CSAdder csadder_2 (
    .A(csadder_1_sum), .B(and_3_out), .clk(Clock1_out), .reset(reset), .Sum(csadder_2_sum), .Ci(out_4[5]));
  and and_5 (and_5_out, in_2[3], in_1[3]);
  and and_6 (and_6_out, in_2[2], in_1[2]);
  CSAdder csadder_3 (
    .A(and_4_out), .B(csadder_2_sum), .clk(Clock1_out), .reset(reset), .Sum(csadder_3_sum), .Ci(out_4[4]));
  and and_7 (and_7_out, in_2[1], in_1[1]);
  CSAdder csadder_4 (
    .A(and_5_out), .B(csadder_3_sum), .clk(Clock1_out), .reset(reset), .Sum(csadder_4_sum), .Ci(out_4[3]));
  and and_8 (and_8_out, in_2[0], in_1[0]);
  CSAdder csadder_5 (
    .A(and_6_out), .B(csadder_4_sum), .clk(Clock1_out), .reset(reset), .Sum(csadder_5_sum), .Ci(out_4[2]));
  CSAdder csadder_6 (
    .A(and_7_out), .B(csadder_5_sum), .clk(Clock1_out), .reset(reset), .Sum(csadder_6_sum), .Ci(out_4[1]));
  CSAdder csadder_7 (.A(and_8_out), .B(csadder_6_sum), .clk(Clock1_out), .reset(reset), .Sum(out_4[0]));  // open: Ci
endmodule

module TCMP (
  input  x,
  input  clk,
  input  reset,
  output S
);

  wire not_1_out;

  not not_1 (not_1_out, x);
  D_Flip_Flop d_ff_1 (.D(not_1_out), .clk(clk), .Q(S), .reset(reset));  // open: Qn, preset
endmodule

module CSAdder (
  input  A,
  input  B,
  input  clk,
  input  reset,
  output Sum,
  output Ci
);

  wire and_1_out, xor_1_out;

  xor xor_1 (xor_1_out, A, B);
  and and_1 (and_1_out, A, B);
  D_Flip_Flop d_ff_1 (.D(xor_1_out), .clk(clk), .Q(Sum), .reset(reset));  // open: Qn, preset
  D_Flip_Flop d_ff_2 (.D(and_1_out), .clk(clk), .Q(Ci), .reset(reset));  // open: Qn, preset

  // Notes on the sheet:
  //   S1
  //   C1
  //   Si
  //   Ci
endmodule
